# Fritzing sketch pic_morse (saved by Fritzing 0.9.3b)
circuit board: 3.65817cm x 3.52582cm
breadboards: 1

parts:
  PIC16F690 = PIC16F690 [part_number=PIC16F690 package="DIP (Dual Inline) [THT]"]
  J1 = PIC ICSP - 5 pins [form="♂ (male)" part_number=iCP01 package=THT]
  Speaker_Connect = female pin header, 2 pins [form="♀ (female)"]
  Reset = Pushbutton [package="[THT]"]

nets:
  N1: PIC16F690.VDD, J1.pin2, Reset.Pin_1, Reset.Pin_2
  N2: PIC16F690.RA3, J1.pin1
  N3: PIC16F690.RC5, Speaker_Connect.pin2
  N4: PIC16F690.RA1, J1.pin5
  N5: PIC16F690.RA0, J1.pin4
  N6: PIC16F690.VSS, J1.pin3, Speaker_Connect.pin1, Reset.Pin_3, Reset.Pin_4

notes:
  +5V
  GND
  PICMorse
  --->

custom parts:
  PIC16F690: PIC® Flash microcontroller mid-range x14 architecture 2.0-5.5 volts, internal oscillator 8 MHz - 32 KHz, EEPROM, nanoWatt Technology. 12 channels of 10-bit A/D, two comparators, on-chip voltage reference, Enhanced Capture/Compare/PWM, EUSART, SPI/I2C.
  PIC ICSP - 5 pins: PIC ICSP programmer connection (ICP01 PICkit 2 sw)

// code stored in the sketch: blinka.c
/* blinka.c  PICkit 2 LPC DS1 or breadboard  */ 
/* B Knudsen Cc5x C-compiler - not ANSI-C */
#include "16F690.h"
#pragma config |= 0x00D4 
void delay10( char );
 
void main( void)
{
  TRISC.0 = 0;  /* PORTC pin 0 output */
  
  while(1)
    {
       delay10(10);
	   PORTC.0 = 1; /* PORTC pin 0 "1" */
	   delay10(10);
	   PORTC.0 = 0; /* PORTC pin 0 "0" */
    }
}


/* *********************************** */
/*            FUNCTIONS                */
/* *********************************** */


void delay10( char n)
/*
  Delays a multiple of 10 milliseconds using the TMR0 timer
  Clock : 4 MHz   => period T = 0.25 microseconds
  1 IS = 1 Instruction Cycle = 1 microsecond
  error: 0.16 percent
*/
{
    char i;

    OPTION = 7;
    do  {
        i = TMR0 + 39; /* 256 microsec * 39 = 10 ms */
        while ( i != TMR0)
            ;
    } while ( --n > 0);
}


/* *********************************** */
/*            HARDWARE                 */
/* *********************************** */

/*
             _____________  _____________ 
            |             \/             |
      +5V---|Vdd        16F690        Vss|---Gnd
            |RA5            RA0/AN0/(PGD)|
            |RA4/AN3            RA1/(PGC)|
            |RA3/!MCLR/(Vpp)  RA2/AN2/INT|
            |RC5/CCP                  RC0|->-LED0
            |RC4                      RC1|
            |RC3/AN7                  RC2|
            |RC6/AN8             AN10/RB4|
            |RC7/AN9               RB5/Rx|
            |RB7/Tx                   RB6|
            |____________________________|
                                          
*/

// code stored in the sketch: hejsan.c
/* hello_blink.c  PICkit 2 breadboard LED + bitbanging com */ 
/* hello_blink.c  PICkit 2 breadboard LED + bitbanging com */ 
/* Blink with LED, receive char and printout loop count    */

/* B Knudsen Cc5x C-compiler - not ANSI-C */
#include <16F690.h>
#include <int16Cxx.h>
#pragma config |= 0x00D4 

/* FUNCTION PROTOTYPES */
void delay10( char );
void init_serial( void );
void putchar( char);
void printf(const char *string, char variable);

/* GLOBAL VARIABLES */
bit receiver_flag;   /* Signal-flag used by interrupt routine   */
char receiver_byte;  /* Transfer Byte used by interrupt routine */

/* INTERRUPT ROUTINE */
/* Interrupt routine - receiving chars at need */ 
#pragma origin 4
interrupt int_server( void ) /* the place for the interrupt routine */
{
  int_save_registers
  /* New interrupts are automaticaly disabled            */
  /* "Interrupt on change" at pin RA1 from PK2 UART-tool */
  
  if( PORTA.1 == 0 )  /* Interpret this as the startbit  */
    {  /* Receive one full character   */
      char bitCount, ti;
      /* delay 1,5 bit 156 usec at 4 MHz         */
      /* 5+28*5-1+1+2+9=156 without optimization */
      ti = 28; do ; while( --ti > 0); nop(); nop2();
      for( bitCount = 8; bitCount > 0 ; bitCount--)
       {
         Carry = PORTA.1;
         receiver_byte = rr( receiver_byte);  /* rotate carry */
         /* delay one bit 104 usec at 4 MHz       */
         /* 5+18*5-1+1+9=104 without optimization */ 
         ti = 18; do ; while( --ti > 0); nop(); 
        }
      receiver_flag = 1; /* A full character is now received */
    }
  RABIF = 0;    /* Reset the RABIF-flag before leaving   */
  int_restore_registers
  /* New interrupts are now enabled */
}


 /* MAIN PROGRAM */
void main( void)
{
    TRISC.0 = 0;   /* PORTC pin 0 output to LED     */
	TRISC.7 = 1;   /* PORTC pin 7 input from Button */
	ANSELH.1 = 0;  /* PORTC pin 7 not analog        */

    init_serial();
    char loopcounter=0;
	char speed = 100;
 
    receiver_flag=0;
  
    IOCA.1 = 1; /* PORTA.1 interrupt on change */
    RABIE =1;   /* interrupt on change         */
    GIE = 1;    /* interrupt enable            */
    
    delay10(100); /* wait one second */	
	printf("\r\nBlinks with LED\r\n",0); 
	printf("Receives char and then printout loop count.\r\n",0);
	printf("Fast blink if button is pressed.\r\n",0);
	
  while(1)
    {
	   if(!PORTC.7) speed=10; else speed=100; 
       delay10(speed);
	   PORTC.0 = 1; /* PORTC pin 0 "1" */
	   delay10(speed);
	   PORTC.0 = 0; /* PORTC pin 0 "0" */
	     if(receiver_flag) 
		   {
		     printf("\r\n", 0);
			 printf("%c ", receiver_byte);
		     printf("Loops = %u\r\n", loopcounter);
			 receiver_flag = 0;
		   }
	   loopcounter++;
    }
}




/* *********************************** */
/*            FUNCTIONS                */
/* *********************************** */

void delay10( char n)
/*
  Delays a multiple of 10 milliseconds using the TMR0 timer
  Clock : 4 MHz   => period T = 0.25 microseconds
  1 IS = 1 Instruction Cycle = 1 microsecond
  error: 0.16 percent
*/
{
    char i;

    OPTION = 7;
    do  {
        i = TMR0 + 39; /* 256 microsec * 39 = 10 ms */
        while ( i != TMR0)
            ;
    } while ( --n > 0);
}

void init_serial( void )  /* initialise PIC16F690 bitbang serialcom */
{
   ANSEL.0 = 0; /* No AD on RA0             */
   ANSEL.1 = 0; /* No AD on RA1             */
   PORTA.0 = 1; /* marking line             */
   TRISA.0 = 0; /* output to PK2 UART-tool  */
   TRISA.1 = 1; /* input from PK2 UART-tool */
   return;      
}

void putchar( char ch )  /* sends one char */
{
  char bitCount, ti;
  PORTA.0 = 0; /* set startbit */
  for ( bitCount = 10; bitCount > 0 ; bitCount-- )
   {
     /* delay one bit 104 usec at 4 MHz       */
     /* 5+18*5-1+1+9=104 without optimization */ 
     ti = 18; do ; while( --ti > 0); nop(); 
     Carry = 1;     /* stopbit                    */
     ch = rr( ch ); /* Rotate Right through Carry */
     PORTA.0 = Carry;
   }
  return;
}

void printf(const char *string, char variable) // printf look-alike
{
  char i, k, m, a, b;
  for(i = 0 ; ; i++)
   {
     k = string[i];
     if( k == '\0') break;   // at end of string
     if( k == '%')           // insert variable in string
      {
        i++;
        k = string[i];
        switch(k)
         {
           case 'd':         // %d  signed 8bit
             if( variable.7 ==1) putchar('-');
             else putchar(' ');
             if( variable > 127) variable = -variable;  // no break!
           case 'u':         // %u unsigned 8bit
             a = variable/100;
             putchar('0'+a); // print 100's
             b = variable%100;
             a = b/10;
             putchar('0'+a); // print 10's
             a = b%10;
             putchar('0'+a); // print 1's
             break;
           case 'x':         // %x HEX 8 bit
             static const char Hex_table[16] = "0123456789ABCDEF" ;
		     a = swap(variable);
             a = a & 0b0000.1111;
             b = Hex_table[a];
             putchar(b);
             a = variable & 0b0000.1111;
             b = Hex_table[a];
             putchar(b);
             break;
           case 'b':         // %b BINARY 8bit
             for( m = 0 ; m < 8 ; m++ )
              {
                if (variable.7 == 1) putchar('1');
                else putchar('0');
                variable = rl(variable);
               }
              break;
           case 'c':         // %c  'char'
             putchar(variable);
             break;
           case '%':
             putchar('%');
             break;
           default:          // not implemented
             putchar('!');
         }
      }
      else putchar(k);
   }
}





/* *********************************** */
/*            HARDWARE                 */
/* *********************************** */

/*
  Serial communication with PK2 UART-tool
  or used with TTL to USB Serial Converter
             _____________  _____________ 
            |             \/             |
      +5V---|Vdd        16F690        Vss|---Gnd
            |RA5            RA0/AN0/(PGD)|bbTx->- PK2 UART-tool
            |RA4/AN3            RA1/(PGC)|bbRx-<- PK2 UART-tool
            |RA3/!MCLR/(Vpp)  RA2/AN2/INT|
            |RC5/CCP                  RC0|->-LED0
            |RC4                      RC1|
            |RC3/AN7                  RC2|
   PullUp   |RC6/AN8             AN10/RB4|
   Butt_n->-|RC7/AN9               RB5/Rx|
            |RB7/Tx                   RB6|
            |____________________________|
			
  UART RB7, RB6 not used by this program		
 
  TTL to USB Serial Converter if used with Frizing serial monitor: 
                 FTDI TTL_232R-5V
          unconnected --- 6 RTS# green
  bbTx->- 1k resistor ->- 5 rxd  yellow TTL_232R-5V
  bbRx-<- 1k resistor -<- 4 txd  orange TTL_232R-5V		
          unconnected --- 3 VCC  red
          unconnected --- 2 CTS# brown
                  Gnd --- 1 GND  black					
*/

// code stored in the sketch: hello_blink.c
/* hello_blink.c  PICkit 2 breadboard LED + bitbanging com */ 
/* Blink with LED, receive char and printout loop count    */

/* B Knudsen Cc5x C-compiler - not ANSI-C */
#include <16F690.h>
#include <int16Cxx.h>
#pragma config |= 0x00D4 

/* FUNCTION PROTOTYPES */
void delay10( char );
void init_serial( void );
void putchar( char);
void printf(const char *string, char variable);

/* GLOBAL VARIABLES */
bit receiver_flag;   /* Signal-flag used by interrupt routine   */
char receiver_byte;  /* Transfer Byte used by interrupt routine */

/* INTERRUPT ROUTINE */
/* Interrupt routine - receiving chars at need */ 
#pragma origin 4
interrupt int_server( void ) /* the place for the interrupt routine */
{
  int_save_registers
  /* New interrupts are automaticaly disabled            */
  /* "Interrupt on change" at pin RA1 from PK2 UART-tool */
  
  if( PORTA.1 == 0 )  /* Interpret this as the startbit  */
    {  /* Receive one full character   */
      char bitCount, ti;
      /* delay 1,5 bit 156 usec at 4 MHz         */
      /* 5+28*5-1+1+2+9=156 without optimization */
      ti = 28; do ; while( --ti > 0); nop(); nop2();
      for( bitCount = 8; bitCount > 0 ; bitCount--)
       {
         Carry = PORTA.1;
         receiver_byte = rr( receiver_byte);  /* rotate carry */
         /* delay one bit 104 usec at 4 MHz       */
         /* 5+18*5-1+1+9=104 without optimization */ 
         ti = 18; do ; while( --ti > 0); nop(); 
        }
      receiver_flag = 1; /* A full character is now received */
    }
  RABIF = 0;    /* Reset the RABIF-flag before leaving   */
  int_restore_registers
  /* New interrupts are now enabled */
}


 /* MAIN PROGRAM */
void main( void)
{
    TRISC.0 = 0;   /* PORTC pin 0 output to LED     */
	TRISC.7 = 1;   /* PORTC pin 7 input from Button */
	ANSELH.1 = 0;  /* PORTC pin 7 not analog        */

    init_serial();
    char loopcounter=0;
	char speed = 100;
 
    receiver_flag=0;
  
    IOCA.1 = 1; /* PORTA.1 interrupt on change */
    RABIE =1;   /* interrupt on change         */
    GIE = 1;    /* interrupt enable            */
    
    delay10(100); /* wait one second */	
	printf("\r\nBlinks with LED\r\n",0); 
	printf("Receives char and then printout loop count.\r\n",0);
	printf("Fast blink if button is pressed.\r\n",0);
	
  while(1)
    {
	   if(!PORTC.7) speed=10; else speed=100; 
       delay10(speed);
	   PORTC.0 = 1; /* PORTC pin 0 "1" */
	   delay10(speed);
	   PORTC.0 = 0; /* PORTC pin 0 "0" */
	     if(receiver_flag) 
		   {
		     printf("\r\n", 0);
			 printf("%c ", receiver_byte);
		     printf("Loops = %u\r\n", loopcounter);
			 receiver_flag = 0;
		   }
	   loopcounter++;
    }
}




/* *********************************** */
/*            FUNCTIONS                */
/* *********************************** */

void delay10( char n)
/*
  Delays a multiple of 10 milliseconds using the TMR0 timer
  Clock : 4 MHz   => period T = 0.25 microseconds
  1 IS = 1 Instruction Cycle = 1 microsecond
  error: 0.16 percent
*/
{
    char i;

    OPTION = 7;
    do  {
        i = TMR0 + 39; /* 256 microsec * 39 = 10 ms */
        while ( i != TMR0)
            ;
    } while ( --n > 0);
}

void init_serial( void )  /* initialise PIC16F690 bitbang serialcom */
{
   ANSEL.0 = 0; /* No AD on RA0             */
   ANSEL.1 = 0; /* No AD on RA1             */
   PORTA.0 = 1; /* marking line             */
   TRISA.0 = 0; /* output to PK2 UART-tool  */
   TRISA.1 = 1; /* input from PK2 UART-tool */
   return;      
}

void putchar( char ch )  /* sends one char */
{
  char bitCount, ti;
  PORTA.0 = 0; /* set startbit */
  for ( bitCount = 10; bitCount > 0 ; bitCount-- )
   {
     /* delay one bit 104 usec at 4 MHz       */
     /* 5+18*5-1+1+9=104 without optimization */ 
     ti = 18; do ; while( --ti > 0); nop(); 
     Carry = 1;     /* stopbit                    */
     ch = rr( ch ); /* Rotate Right through Carry */
     PORTA.0 = Carry;
   }
  return;
}

void printf(const char *string, char variable) // printf look-alike
{
  char i, k, m, a, b;
  for(i = 0 ; ; i++)
   {
     k = string[i];
     if( k == '\0') break;   // at end of string
     if( k == '%')           // insert variable in string
      {
        i++;
        k = string[i];
        switch(k)
         {
           case 'd':         // %d  signed 8bit
             if( variable.7 ==1) putchar('-');
             else putchar(' ');
             if( variable > 127) variable = -variable;  // no break!
           case 'u':         // %u unsigned 8bit
             a = variable/100;
             putchar('0'+a); // print 100's
             b = variable%100;
             a = b/10;
             putchar('0'+a); // print 10's
             a = b%10;
             putchar('0'+a); // print 1's
             break;
           case 'x':         // %x HEX 8 bit
             static const char Hex_table[16] = "0123456789ABCDEF" ;
		     a = swap(variable);
             a = a & 0b0000.1111;
             b = Hex_table[a];
             putchar(b);
             a = variable & 0b0000.1111;
             b = Hex_table[a];
             putchar(b);
             break;
           case 'b':         // %b BINARY 8bit
             for( m = 0 ; m < 8 ; m++ )
              {
                if (variable.7 == 1) putchar('1');
                else putchar('0');
                variable = rl(variable);
               }
              break;
           case 'c':         // %c  'char'
             putchar(variable);
             break;
           case '%':
             putchar('%');
             break;
           default:          // not implemented
             putchar('!');
         }
      }
      else putchar(k);
   }
}





/* *********************************** */
/*            HARDWARE                 */
/* *********************************** */

/*
  Serial communication with PK2 UART-tool
  or used with TTL to USB Serial Converter
             _____________  _____________ 
            |             \/             |
      +5V---|Vdd        16F690        Vss|---Gnd
            |RA5            RA0/AN0/(PGD)|bbTx->- PK2 UART-tool
            |RA4/AN3            RA1/(PGC)|bbRx-<- PK2 UART-tool
            |RA3/!MCLR/(Vpp)  RA2/AN2/INT|
            |RC5/CCP                  RC0|->-LED0
            |RC4                      RC1|
            |RC3/AN7                  RC2|
   PullUp   |RC6/AN8             AN10/RB4|
   Butt_n->-|RC7/AN9               RB5/Rx|
            |RB7/Tx                   RB6|
            |____________________________|
			
  UART RB7, RB6 not used by this program		
 
  TTL to USB Serial Converter if used with Frizing serial monitor: 
                 FTDI TTL_232R-5V
          unconnected --- 6 RTS# green
  bbTx->- 1k resistor ->- 5 rxd  yellow TTL_232R-5V
  bbRx-<- 1k resistor -<- 4 txd  orange TTL_232R-5V		
          unconnected --- 3 VCC  red
          unconnected --- 2 CTS# brown
                  Gnd --- 1 GND  black					
*/

// code stored in the sketch: hello_blink.ino


// code stored in the sketch: hello_blink_TMP.ino

/*  Compile with  PK2CC5X Tool chain
https://github.com/willsandy/Fritzing-PK2-Cc5x  */ 

/* hello_blink.c  PICkit 2 breadboard LED + bitbanging com    */
/* Program for testing components on breadboard               */ 
/* Blink with LED, serial menu LED on/off blink +/- Sw status */

/* B Knudsen Cc5x C-compiler - not ANSI-C */
#include <16F690.h>
#include <int16Cxx.h>
#pragma config |= 0x00D4 

/* FUNCTION PROTOTYPES */
void delay10( char );
void init_serial( void );
void putchar( char);
void printf(const char *string, char variable);

/* GLOBAL VARIABLES */
bit receiver_flag;   /* Signal-flag used by interrupt routine   */
char receiver_byte;  /* Transfer Byte used by interrupt routine */


/* INTERRUPT ROUTINE */
/* Interrupt routine - receiving chars at need */ 
#pragma origin 4
interrupt int_server( void ) /* the place for the interrupt routine */
{
  int_save_registers
  /* New interrupts are automaticaly disabled            */
  /* "Interrupt on change" at pin RA1 from PK2 UART-tool */
  
  if( PORTA.1 == 0 )  /* Interpret this as the startbit  */
    {  /* Receive one full character   */
      char bitCount, ti;
      /* delay 1,5 bit 156 usec at 4 MHz         */
      /* 5+28*5-1+1+2+9=156 without optimization */
      ti = 28; do ; while( --ti > 0); nop(); nop2();
      for( bitCount = 8; bitCount > 0 ; bitCount--)
       {
         Carry = PORTA.1;
         receiver_byte = rr( receiver_byte);  /* rotate carry */
         /* delay one bit 104 usec at 4 MHz       */
         /* 5+18*5-1+1+9=104 without optimization */ 
         ti = 18; do ; while( --ti > 0); nop(); 
        }
      receiver_flag = 1; /* A full character is now received */
    }
  RABIF = 0;    /* Reset the RABIF-flag before leaving   */
  int_restore_registers
  /* New interrupts are now enabled */
}



 /* MAIN PROGRAM */

void main( void)
{
    /* Initialisations */

  TRISC.0 = 0;   /* PORTC pin 0 output to LED     */
	TRISC.7 = 1;   /* PORTC pin 7 input from Button */
	ANSELH.1 = 0;  /* PORTC pin 7 not analog        */

  init_serial();
	char speed = 100;
  char period;
	char choice;
  bit blink=1;
  receiver_flag=0;
  
  IOCA.1 = 1; /* PORTA.1 interrupt on change */
  RABIE =1;   /* interrupt on change         */
  GIE = 1;    /* interrupt enable            */
    
    /* Main loop  */

	while(1)
   {
     if( receiver_flag ) /* Character received? */ 
      {
        choice = receiver_byte;
        receiver_flag = 0; /* Character now taken */
		/* menu alternatives */
        switch (choice)
         {
          case 'l':
          case 'L':
            printf("\r\n%c LED ON\r\n", choice);
	          PORTC.0 = 1; /* PORTC pin 0 "1" */
            blink=0;
            break;
          case 'o':
          case 'O':
            printf("\r\n%c LED OFF\r\n", choice);
  	        PORTC.0 = 0; /* PORTC pin 0 "0" */
            blink=0;
            break;
          case 'b':
          case 'B':
            blink=1;
            printf("\r\n%c LED BLINK\r\n", choice);
            break;
          case 'S':
          case 's':
	          if(!PORTC.7) printf("\r\n%c Switch is ON/pressed\r\n", choice);
            else printf("\r\n%c Switch is OFF/unpressed\r\n", choice);
            break;
          case '-':
            if(period > 20) period -=10;
            else period = 10;
            printf("\r\n%c ", choice);
            printf("Dec delay %u\r\n", period);
		        blink = 1;
            break;
          case '+':
            if(period < 240) period +=10;
            else period = 250;
            printf("\r\n%c ", choice);
            printf("Inc delay %u\r\n", period);
		        blink = 1;
            break;
          default:
            printf("\r\n%c (L)ed On, led (O)ff, led (B)link, ",choice);
		        printf("(S)witch, delay (+),(-)\r\n",0);
         }
      }

      /* Button action fast blink */
 	  if(PORTC.7) speed = period; else speed = 10;
	  
      /* blink the led with different period */
	  if( blink )
        {  
          delay10(speed);
    	    PORTC.0 = 1; /* PORTC pin 0 "1" */
    	    delay10(speed);
    	    PORTC.0 = 0; /* PORTC pin 0 "0" */
        }

   }

}




/* *********************************** */
/*            FUNCTIONS                */
/* *********************************** */

void delay10( char n)
/*
  Delays a multiple of 10 milliseconds using the TMR0 timer
  Clock : 4 MHz   => period T = 0.25 microseconds
  1 IS = 1 Instruction Cycle = 1 microsecond
  error: 0.16 percent
*/
{
    char i;

    OPTION = 7;
    do  {
          i = TMR0 + 39; /* 256 microsec * 39 = 10 ms */
          while ( i != TMR0)
            ;
        } while ( --n > 0);
}


void init_serial( void )  /* initialise PIC16F690 bitbang serialcom */
{
   ANSEL.0 = 0; /* No AD on RA0             */
   ANSEL.1 = 0; /* No AD on RA1             */
   PORTA.0 = 1; /* marking line             */
   TRISA.0 = 0; /* output to PK2 UART-tool  */
   TRISA.1 = 1; /* input from PK2 UART-tool */
   return;      
}



void putchar( char ch )  /* sends one char */
{
  char bitCount, ti;
  PORTA.0 = 0; /* set startbit */
  for ( bitCount = 10; bitCount > 0 ; bitCount-- )
   {
     /* delay one bit 104 usec at 4 MHz       */
     /* 5+18*5-1+1+9=104 without optimization */ 
     ti = 18; do ; while( --ti > 0); nop(); 
     Carry = 1;     /* stopbit                    */
     ch = rr( ch ); /* Rotate Right through Carry */
     PORTA.0 = Carry;
   }
  return;
}



void printf(const char *string, char variable) // printf look-alike
{
  char i, k, m, a, b;
  for(i = 0 ; ; i++)
   {
     k = string[i];
     if( k == '\0') break;   // at end of string

     if( k == '%')           // insert variable in string
      {
        i++;
        k = string[i];
        switch(k)
         {
           case 'd':         // %d  signed 8bit
             if( variable.7 ==1) putchar('-');
             else putchar(' ');
             if( variable > 127) variable = -variable;  // no break!
           case 'u':         // %u unsigned 8bit
             a = variable/100;
             putchar('0'+a); // print 100's
             b = variable%100;
             a = b/10;
             putchar('0'+a); // print 10's
             a = b%10;
             putchar('0'+a); // print 1's
             break;
           case 'x':         // %x HEX 8 bit
             static const char Hex_table[16] = "0123456789ABCDEF" ;
             a = swap(variable);
             a = a & 0b0000.1111;
             b = Hex_table[a];
             putchar(b);
             a = variable & 0b0000.1111;
             b = Hex_table[a];
             putchar(b);
             break;
           case 'b':         // %b BINARY 8bit
             for( m = 0 ; m < 8 ; m++ )
              {
                if (variable.7 == 1) putchar('1');
                else putchar('0');
                variable = rl(variable);
              }
             break;
           case 'c':         // %c  'char'
             putchar(variable);
             break;
           case '%':
             putchar('%');
             break;
           default:          // not implemented
             putchar('!');
         }
       }
      else putchar(k);
   }

}







/* *********************************** */
/*            HARDWARE                 */
/* *********************************** */

/*
  Serial communication with PK2 UART-tool
  or used with TTL to USB Serial Converter
             _____________  _____________ 
            |             \/             |
      +5V---|Vdd        16F690        Vss|---Gnd
            |RA5            RA0/AN0/(PGD)|bbTx->- PK2 UART-tool
            |RA4/AN3            RA1/(PGC)|bbRx-<- PK2 UART-tool
            |RA3/!MCLR/(Vpp)  RA2/AN2/INT|
            |RC5/CCP                  RC0|->-LED0
            |RC4                      RC1|
            |RC3/AN7                  RC2|
   PullUp   |RC6/AN8             AN10/RB4|
   Butt_n->-|RC7/AN9               RB5/Rx|
            |RB7/Tx                   RB6|
            |____________________________|
			
  UART RB7, RB6 not used by this program		
 
  TTL to USB Serial Converter if used with Frizing serial monitor: 
                 FTDI TTL_232R-5V
          unconnected --- 6 RTS# green
  bbTx->- 1k resistor ->- 5 rxd  yellow TTL_232R-5V
  bbRx-<- 1k resistor -<- 4 txd  orange TTL_232R-5V		
          unconnected --- 3 VCC  red
          unconnected --- 2 CTS# brown
                  Gnd --- 1 GND  black					
*/

// code stored in the sketch: PICMorse.c.ino
/* project.c                  */
/* PIC16F690 compiled with B. Knudsen Cc5x Free, not ANSI-C */

#include "16F690.h"
#include "int16Cxx.h"
#pragma config |= 0x00D4
#pragma char X @ 0x115

void delay( char);
void init_io_ports( void );
void init_serial( void );
void init_interrupt( void );
void putchar( char);
void printf(const char *string, char variable);

bit receiver_flag;   /* Signal-flag used by interrupt routine   */
char receiver_byte;  /* Transfer Byte used by interrupt routine */

#pragma origin 4
interrupt int_server( void ) /* the place for the interrupt routine */
{
  int_save_registers
  /* New interrupts are automaticaly disabled            */
  /* "Interrupt on change" at pin RA1 from PK2 UART-tool */
  
  if( PORTA.1 == 0 )  /* Interpret this as the startbit  */
    {  /* Receive one full character   */
      char bitCount, ti;
      /* delay 1,5 bit 156 usec at 4 MHz         */
      /* 5+28*5-1+1+2+9=156 without optimization */
      ti = 28; do ; while( --ti > 0); nop(); nop2();
      for( bitCount = 8; bitCount > 0 ; bitCount--)
       {
         Carry = PORTA.1;
         receiver_byte = rr( receiver_byte);  /* rotate carry */
         /* delay one bit 104 usec at 4 MHz       */
         /* 5+18*5-1+1+9=104 without optimization */ 
         ti = 18; do ; while( --ti > 0); nop(); 
        }
      receiver_flag = 1; /* A full character is now received */
    }
  RABIF = 0;    /* Reset the RABIF-flag before leaving   */
  int_restore_registers
  /* New interrupts are now enabled */
  
}

#include "math16.h"

#define SPACING_LENGTH 100 // The time (in ms) which it takes 
#define TIME_CONSTANT 70 // A percentage amount of tempo to actually give the playback (Speed up/slow down)

typedef enum
{
	DOT = 50,
	DASH = 150,
	_ = 0
} BeepLength;

void beep_for_time( char ms ){
    TRISC.5 = 0;              /* CCP1 output             */
	delay(ms);
	TRISC.5 = 1;              /* CCP1 output             */
}

void beep_letter( BeepLength slot1, BeepLength slot2, BeepLength slot3, BeepLength slot4 ){	
	if (slot1 == _) return;
	beep_for_time(slot1);
	delay(SPACING_LENGTH); 
	
	if (slot2 == _) return;
	beep_for_time(slot2);
	delay(SPACING_LENGTH); 
	
	if (slot3 == _) return;
	beep_for_time(slot3);
	delay(SPACING_LENGTH); 
	
	if (slot4 == _) return;
	beep_for_time(slot4);
	delay(SPACING_LENGTH); 
}

void main( void) { 
	init_io_ports();
	init_serial();
	init_interrupt();

  	TRISC.5 = 1;              /* CCP1 output             */
	CCP1CON = 0b00.00.1100;   /* PWM-mode                */
	T2CON   = 0b00000.1.00;   /* prescale 1:1            */
	PR2     = 255;            /* max value               */
	CCPR1L = 100; /* change this to your measured value  */  
			
	while(1)
	{
		receiver_flag = 0; 
		receiver_byte = 0;
		
		char text_input[20];
		int text_length = 0;

		printf("\r\nEnter text for translation:  ", 0);
		
		while( receiver_byte != '\n' ) 
		{	
			/* Wait for a character to be received from UART */ 
			while (!receiver_flag);
			receiver_flag = 0; 
		
			text_input[text_length] = receiver_byte;
			text_length++;
		}
		
		if (text_length){
			printf("\r\nTranslating message:  ", 0);
			
			int pos;
			for (pos = 0; pos < text_length; pos++){
				printf("\r %c ", text_input[pos]);
				switch (text_input[pos]){
					case 'a':	
						beep_letter(DOT, DASH, _, _);
						break;
						
					case 'b':	
						beep_letter(DASH, DOT, DOT, DOT);
						break;
						
					case 'c':
						beep_letter(DASH, DOT, DASH, DOT);
						break;
						
					case 'd':
						beep_letter(DASH, DOT, DOT, _);
						break;
						
					case 'e':
						beep_letter(DOT,_,_,_);
						break;
					
					case 'f':
						beep_letter(DOT, DOT, DASH, DOT);
						break;
					
					case 'g':
						beep_letter(DASH, DASH, DOT, _);
						break;
						
					case 'h':
						beep_letter(DOT,DOT,DOT,DOT);
						break;
						
					case 'i':
						beep_letter(DOT, DOT, _, _);
						break;
						
					case 'j':
						beep_letter(DOT, DASH, DASH, DASH);
						break;
						
					case 'k':
						beep_letter(DASH, DOT, DASH, _);
						break;
						
					case 'l':
						beep_letter(DOT,DASH,DOT,DOT);
						break;
						
					case 'm':
						beep_letter(DASH,DASH, _,_);
						break;
						
					case 'n':
						beep_letter(DASH, DOT, _, _);
						break;
						
					case 'o':
						beep_letter(DASH, DASH, DASH, _);
						break;
						
					case 'p':
						beep_letter(DOT, DASH, DASH, DOT);
						break;
						
					case 'q':
						beep_letter(DASH, DASH, DOT, DASH);
						break;
						
					case 'r':
						beep_letter(DOT, DASH, DOT, _);
						break;
						
					case 's':
						beep_letter(DOT, DOT, DOT, _);
						break;
						
					case 't':
						beep_letter(DASH, _,_,_);
						break;
						
					case 'u':
						beep_letter(DOT, DOT, DASH, _);
						break;
						
					case 'v':
						beep_letter(DOT, DOT, DOT, DASH);
						break;
						
					case 'w':
						beep_letter(DOT, DASH, DASH, _);
						break;
						
					case 'x':
						beep_letter(DASH, DOT, DOT, DASH);
						break;
						
					case 'y':
						beep_letter(DASH, DOT, DASH, DASH);
						break;
						
					case 'z': 
						beep_letter(DASH, DASH, DOT, DOT);
						break;
					

					default:
						continue;
				}
			}
			
			printf("\r\n", 0);
		}
	}
}

void delay( char millisec) {
	millisec *= 100 / TIME_CONSTANT;
	
    OPTION = 2;  /* prescaler divide by 8        */
    do  {  TMR0 = 0;
           while ( TMR0 < 125)   /* 125 * 8 = 1000  */ ;
        } while ( -- millisec > 0);
}

void init_io_ports( void ) {
  TRISC = 0xF8; /* 11111000 0 is for outputbit  */
  PORTC = 0b000;    /* initial value */

  ANSEL =0;     /* not AD-input      */
  TRISA.5 = 1;  /* input rpgA        */
  TRISA.4 = 1;  /* input rpgB        */
  /* Enable week pullup's            */
  OPTION.7 = 0; /* !RABPU bit        */
  WPUA.5   = 1; /* rpgA pullup       */
  WPUA.4   = 1; /* rpgB pullup       */
  X.6 = 1;
  TRISB.6 = 1;  /* PORTB pin 6 input */
  
  return;
}

void init_serial( void )  /* initialise PIC16F690 bitbang serialcom */ {
   ANSEL.0 = 0; /* No AD on RA0             */
   ANSEL.1 = 0; /* No AD on RA1             */
   PORTA.0 = 1; /* marking line             */
   TRISA.0 = 0; /* output to PK2 UART-tool  */
   TRISA.1 = 1; /* input from PK2 UART-tool */
   receiver_flag = 0 ;
   return;      
}

void init_interrupt( void ) {
  IOCA.1 = 1; /* PORTA.1 interrupt on change */
  RABIE =1;   /* interrupt on change         */
  GIE = 1;    /* interrupt enable            */
  return;
}

void putchar( char ch )  /* sends one char */ {
  char bitCount, ti;
  PORTA.0 = 0; /* set startbit */
  for ( bitCount = 10; bitCount > 0 ; bitCount-- )
   {
     /* delay one bit 104 usec at 4 MHz       */
     /* 5+18*5-1+1+9=104 without optimization */ 
     ti = 18; do ; while( --ti > 0); nop(); 
     Carry = 1;     /* stopbit                    */
     ch = rr( ch ); /* Rotate Right through Carry */
     PORTA.0 = Carry;
   }
  return;
}

void printf(const char *string, char variable){
  char i, k, m, a, b;
  for(i = 0 ; ; i++)
   {
     k = string[i];
     if( k == '\0') break;   // at end of string
     if( k == '%')           // insert variable in string
      {
        i++;
        k = string[i];
        switch(k)
         {
           case 'd':         // %d  signed 8bit
             if( variable.7 ==1) putchar('-');
             else putchar(' ');
             if( variable > 127) variable = -variable;  // no break!
           case 'u':         // %u unsigned 8bit
             a = variable/100;
             putchar('0'+a); // print 100's
             b = variable%100;
             a = b/10;
             putchar('0'+a); // print 10's
             a = b%10;
             putchar('0'+a); // print 1's
             break;
           case 'b':         // %b BINARY 8bit
             for( m = 0 ; m < 8 ; m++ )
              {
                if (variable.7 == 1) putchar('1');
                else putchar('0');
                variable = rl(variable);
               }
              break;
           case 'c':         // %c  'char'
             putchar(variable);
             break;
           case '%':
             putchar('%');
             break;
           default:          // not implemented
             putchar('!');
         }
      }
      else putchar(k);
   }
}

// code stored in the sketch: Untitled5.ino
/* project.c                  */
/* PIC16F690 compiled with B. Knudsen Cc5x Free, not ANSI-C */

#include "16F690.h"
#include "int16Cxx.h"
#pragma config |= 0x00D4
#pragma char X @ 0x115

void delay( char);
void init_io_ports( void );
void init_serial( void );
void init_interrupt( void );
void putchar( char);
void printf(const char *string, char variable);

bit receiver_flag;   /* Signal-flag used by interrupt routine   */
char receiver_byte;  /* Transfer Byte used by interrupt routine */

#pragma origin 4
interrupt int_server( void ) /* the place for the interrupt routine */
{
  int_save_registers
  /* New interrupts are automaticaly disabled            */
  /* "Interrupt on change" at pin RA1 from PK2 UART-tool */
  
  if( PORTA.1 == 0 )  /* Interpret this as the startbit  */
    {  /* Receive one full character   */
      char bitCount, ti;
      /* delay 1,5 bit 156 usec at 4 MHz         */
      /* 5+28*5-1+1+2+9=156 without optimization */
      ti = 28; do ; while( --ti > 0); nop(); nop2();
      for( bitCount = 8; bitCount > 0 ; bitCount--)
       {
         Carry = PORTA.1;
         receiver_byte = rr( receiver_byte);  /* rotate carry */
         /* delay one bit 104 usec at 4 MHz       */
         /* 5+18*5-1+1+9=104 without optimization */ 
         ti = 18; do ; while( --ti > 0); nop(); 
        }
      receiver_flag = 1; /* A full character is now received */
    }
  RABIF = 0;    /* Reset the RABIF-flag before leaving   */
  int_restore_registers
  /* New interrupts are now enabled */
  
}

#include "math16.h"

#define SPACING_LENGTH 100 // The time (in ms) which it takes 
#define TIME_CONSTANT 70 // A percentage amount of tempo to actually give the playback (Speed up/slow down)

typedef enum
{
	DOT = 50,
	DASH = 150,
	_ = 0
} BeepLength;

void beep_for_time( char ms ){
    TRISC.5 = 0;              /* CCP1 output             */
	delay(ms);
	TRISC.5 = 1;              /* CCP1 output             */
}

void beep_letter( BeepLength slot1, BeepLength slot2, BeepLength slot3, BeepLength slot4 ){	
	if (slot1 == _) return;
	beep_for_time(slot1);
	delay(SPACING_LENGTH); 
	
	if (slot2 == _) return;
	beep_for_time(slot2);
	delay(SPACING_LENGTH); 
	
	if (slot3 == _) return;
	beep_for_time(slot3);
	delay(SPACING_LENGTH); 
	
	if (slot4 == _) return;
	beep_for_time(slot4);
	delay(SPACING_LENGTH); 
}

void main( void) { 
	init_io_ports();
	init_serial();
	init_interrupt();

  	TRISC.5 = 1;              /* CCP1 output             */
	CCP1CON = 0b00.00.1100;   /* PWM-mode                */
	T2CON   = 0b00000.1.00;   /* prescale 1:1            */
	PR2     = 255;            /* max value               */
	CCPR1L = 100; /* change this to your measured value  */  
			
	while(1)
	{
		receiver_flag = 0; 
		receiver_byte = 0;
		
		char text_input[20];
		int text_length = 0;

		printf("\r\nEnter text for translation:  ", 0);
		
		while( receiver_byte != '\n' ) 
		{	
			/* Wait for a character to be received from UART */ 
			while (!receiver_flag);
			receiver_flag = 0; 
		
			text_input[text_length] = receiver_byte;
			text_length++;
		}
		
		if (text_length){
			printf("\r\nTranslating message:  ", 0);
			
			int pos;
			for (pos = 0; pos < text_length; pos++){
				printf("\r %c ", text_input[pos]);
				switch (text_input[pos]){
					case 'a':	
						beep_letter(DOT, DASH, _, _);
						break;
						
					case 'b':	
						beep_letter(DASH, DOT, DOT, DOT);
						break;
						
					case 'c':
						beep_letter(DASH, DOT, DASH, DOT);
						break;
						
					case 'd':
						beep_letter(DASH, DOT, DOT, _);
						break;
						
					case 'e':
						beep_letter(DOT,_,_,_);
						break;
					
					case 'f':
						beep_letter(DOT, DOT, DASH, DOT);
						break;
					
					case 'g':
						beep_letter(DASH, DASH, DOT, _);
						break;
						
					case 'h':
						beep_letter(DOT,DOT,DOT,DOT);
						break;
						
					case 'i':
						beep_letter(DOT, DOT, _, _);
						break;
						
					case 'j':
						beep_letter(DOT, DASH, DASH, DASH);
						break;
						
					case 'k':
						beep_letter(DASH, DOT, DASH, _);
						break;
						
					case 'l':
						beep_letter(DOT,DASH,DOT,DOT);
						break;
						
					case 'm':
						beep_letter(DASH,DASH, _,_);
						break;
						
					case 'n':
						beep_letter(DASH, DOT, _, _);
						break;
						
					case 'o':
						beep_letter(DASH, DASH, DASH, _);
						break;
						
					case 'p':
						beep_letter(DOT, DASH, DASH, DOT);
						break;
						
					case 'q':
						beep_letter(DASH, DASH, DOT, DASH);
						break;
						
					case 'r':
						beep_letter(DOT, DASH, DOT, _);
						break;
						
					case 's':
						beep_letter(DOT, DOT, DOT, _);
						break;
						
					case 't':
						beep_letter(DASH, _,_,_);
						break;
						
					case 'u':
						beep_letter(DOT, DOT, DASH, _);
						break;
						
					case 'v':
						beep_letter(DOT, DOT, DOT, DASH);
						break;
						
					case 'w':
						beep_letter(DOT, DASH, DASH, _);
						break;
						
					case 'x':
						beep_letter(DASH, DOT, DOT, DASH);
						break;
						
					case 'y':
						beep_letter(DASH, DOT, DASH, DASH);
						break;
						
					case 'z': 
						beep_letter(DASH, DASH, DOT, DOT);
						break;
					

					default:
						continue;
				}
			}
			
			printf("\r\n", 0);
		}
	}
}

void delay( char millisec) {
	millisec *= 100 / TIME_CONSTANT;
	
    OPTION = 2;  /* prescaler divide by 8        */
    do  {  TMR0 = 0;
           while ( TMR0 < 125)   /* 125 * 8 = 1000  */ ;
        } while ( -- millisec > 0);
}

void init_io_ports( void ) {
  TRISC = 0xF8; /* 11111000 0 is for outputbit  */
  PORTC = 0b000;    /* initial value */

  ANSEL =0;     /* not AD-input      */
  TRISA.5 = 1;  /* input rpgA        */
  TRISA.4 = 1;  /* input rpgB        */
  /* Enable week pullup's            */
  OPTION.7 = 0; /* !RABPU bit        */
  WPUA.5   = 1; /* rpgA pullup       */
  WPUA.4   = 1; /* rpgB pullup       */
  X.6 = 1;
  TRISB.6 = 1;  /* PORTB pin 6 input */
  
  return;
}

void init_serial( void )  /* initialise PIC16F690 bitbang serialcom */ {
   ANSEL.0 = 0; /* No AD on RA0             */
   ANSEL.1 = 0; /* No AD on RA1             */
   PORTA.0 = 1; /* marking line             */
   TRISA.0 = 0; /* output to PK2 UART-tool  */
   TRISA.1 = 1; /* input from PK2 UART-tool */
   receiver_flag = 0 ;
   return;      
}

void init_interrupt( void ) {
  IOCA.1 = 1; /* PORTA.1 interrupt on change */
  RABIE =1;   /* interrupt on change         */
  GIE = 1;    /* interrupt enable            */
  return;
}

void putchar( char ch )  /* sends one char */ {
  char bitCount, ti;
  PORTA.0 = 0; /* set startbit */
  for ( bitCount = 10; bitCount > 0 ; bitCount-- )
   {
     /* delay one bit 104 usec at 4 MHz       */
     /* 5+18*5-1+1+9=104 without optimization */ 
     ti = 18; do ; while( --ti > 0); nop(); 
     Carry = 1;     /* stopbit                    */
     ch = rr( ch ); /* Rotate Right through Carry */
     PORTA.0 = Carry;
   }
  return;
}

void printf(const char *string, char variable){
  char i, k, m, a, b;
  for(i = 0 ; ; i++)
   {
     k = string[i];
     if( k == '\0') break;   // at end of string
     if( k == '%')           // insert variable in string
      {
        i++;
        k = string[i];
        switch(k)
         {
           case 'd':         // %d  signed 8bit
             if( variable.7 ==1) putchar('-');
             else putchar(' ');
             if( variable > 127) variable = -variable;  // no break!
           case 'u':         // %u unsigned 8bit
             a = variable/100;
             putchar('0'+a); // print 100's
             b = variable%100;
             a = b/10;
             putchar('0'+a); // print 10's
             a = b%10;
             putchar('0'+a); // print 1's
             break;
           case 'b':         // %b BINARY 8bit
             for( m = 0 ; m < 8 ; m++ )
              {
                if (variable.7 == 1) putchar('1');
                else putchar('0');
                variable = rl(variable);
               }
              break;
           case 'c':         // %c  'char'
             putchar(variable);
             break;
           case '%':
             putchar('%');
             break;
           default:          // not implemented
             putchar('!');
         }
      }
      else putchar(k);
   }
}
